# Fritzing sketch PG5500 - Alarm clock - TFT ST7735 - RTC DS1307 (saved by Fritzing 0.9.3b)
breadboards: 1

parts:
  TFT1 = 2.2" TFT with MicroSD Breakout
  Part1 = Arduino Uno (Rev3)
  Tiny_RTC1 = Tiny RTC
  RESET = Pushbutton [package="[THT]"]
  SET_ALARM = Pushbutton [package="[THT]"]
  R2 = Resistor [tolerance=±5% resistance=10k package="0805 [SMD]"]
  R1 = Resistor [tolerance=±5% resistance=10k package="1206 [SMD]"]
  R1_2 = Resistor [tolerance=±5% resistance=10k package="2010 [SMD]"]
  R3 = Resistor [tolerance=±5% resistance=220 package=THT]
  J1 = Piezo Speaker
  HOURS_KNOB = POT [package=pot_alpha_rv16af-20]
  MINUTES_KNOB = POT [package=pot_alpha_rv16af-20]

nets:
  N1: TFT1.SCK, Part1.D13/SCK
  N2: TFT1.MOSI, Part1.D11_PWM/MOSI
  N3: TFT1.CS, Part1.D10_PWM/SS
  N4: TFT1.SDCS, Part1.D9_PWM
  N5: TFT1.RST, Part1.D8
  VIN: TFT1.VIN, Part1.5V, Tiny_RTC1.VCC, RESET.Pin_3, RESET.Pin_4, SET_ALARM.Pin_3, SET_ALARM.Pin_4, HOURS_KNOB.A, MINUTES_KNOB.A
  GND: TFT1.GND, Part1.GND, Tiny_RTC1.GND, R2.Pin_0, R1.Pin_0, R1_2.Pin_0, R3.Pin_0, HOURS_KNOB.E, MINUTES_KNOB.E
  N6: Part1.A0, HOURS_KNOB.S
  N7: Part1.A1, MINUTES_KNOB.S
  N8: Part1.A4/SDA, Tiny_RTC1.SDA
  N9: Part1.A5/SCL, Tiny_RTC1.SCL
  N10: Part1.D2, RESET.Pin_1, RESET.Pin_2, R2.Pin_1
  N11: Part1.D3_PWM, SET_ALARM.Pin_1, SET_ALARM.Pin_2, R1.Pin_1, R1_2.Pin_1
  N12: Part1.D4, J1.pin2
  N13: R3.Pin_1, J1.pin1

custom parts:
  2.2" TFT with MicroSD Breakout: 2.2" TFT Display with HX8340B Controller and MicroSD Card
  Tiny RTC: Tiny RTC I2C module DS1370Z RTC and AT24C32 EEPROM
